// Logisim project part2log.circ as structural Verilog: 1 circuit, main circuit main
module main (
  input  a,
  input  b,
  input  c,
  input  d
);

  wire nand_1_out, nand_2_out, nand_3_out, nand_4_out, nand_5_out, nand_6_out, not_1_out, not_2_out,
       not_3_out, not_4_out;

  not not_1 (not_1_out, a);
  not not_2 (not_2_out, b);
  not not_3 (not_3_out, c);
  nand nand_1 (nand_1_out, not_1_out, not_2_out, not_3_out);
  nand nand_2 (nand_2_out, c, d);
  nand nand_3 (nand_3_out, b, d);
  nand nand_4 (nand_4_out, a, b, not_3_out);
  nand nand_5 (nand_5_out, nand_1_out, nand_2_out, nand_3_out);
  not not_4 (not_4_out, nand_5_out);
  nand nand_6 (nand_6_out, not_4_out, nand_4_out);
  LED led_1 (.in(nand_6_out));
  LED led_2 (.in(nand_6_out));

  // Notes on the sheet:
  //   LED Monitors
  //   High
  //   Low
endmodule
