// Logisim project part4log2.circ as structural Verilog: 1 circuit, main circuit main
module main (
  input  a,
  input  b,
  input  c
);

  wire decoder_1_out0, decoder_1_out6, decoder_1_out7, not_1_out, not_2_out, not_3_out, or_1_out, or_2_out;

  Decoder #(.select(3), .enable("false")) decoder_1 (
    .out0(decoder_1_out0), .out6(decoder_1_out6), .out7(decoder_1_out7), .sel({a, b, c}));  // open: out1, out2, out3, out4, out5
  not not_1 (not_1_out, decoder_1_out6);
  not not_2 (not_2_out, decoder_1_out7);
  not not_3 (not_3_out, decoder_1_out0);
  or or_1 (or_1_out, not_1_out, not_2_out);
  LED led_1 (.in(or_2_out));
  or or_2 (or_2_out, not_3_out, or_1_out);
  LED led_2 (.in(or_2_out));

  // Notes on the sheet:
  //   Inputs
  //   Logic Monitors
  //   High
  //   Low
endmodule
